// Logisim project cpu.circ as structural Verilog: 5 circuits, main circuit main
module main (
  input  [3:0] ALU_op,
  input  [1:0] A_src,
  input  [1:0] B_src,
  input  C_write,
  input  data_src,
  input  X_write,
  input  [1:0] addr_src,
  input  [1:0] ACCUM_src,
  input  ACCUM_write,
  input  oper_write,
  input  IR_write,
  input  PC_write,
  input  mem_write
);

  wire alu_1_c_out, alu_1_n, alu_1_v, alu_1_z, CLOCK_out, d_ff_1_q, not_1_out;
  wire [7:0] STATE_q;
  wire [15:0] ACCUM_q, alu_1_result, IR_q, multiplexer_1_out, multiplexer_2_out, multiplexer_3_out,
       multiplexer_4_out, multiplexer_5_out, OPER_q, PC_q, ram_1_data, rom_1_data, X_q;

  Clock CLOCK (.out(CLOCK_out));
  Register #(.width(16)) PC (.D(alu_1_result), .en(PC_write), .Q(PC_q), .clk(CLOCK_out));  // open: clr
  Register STATE (.Q(STATE_q), .clk(CLOCK_out));  // open: D, en, clr
  Multiplexer #(.select(2), .width(16)) multiplexer_1 (
    .in0(ACCUM_q), .in1(PC_q), .out(multiplexer_1_out), .sel(A_src));  // open: in2, in3
  Multiplexer #(.width(16)) multiplexer_2 (.in0(ACCUM_q), .in1(alu_1_result), .out(multiplexer_2_out), .sel(data_src));
  Multiplexer #(.select(2), .width(16)) multiplexer_3 (
    .in0(PC_q), .in1(OPER_q), .out(multiplexer_3_out), .sel(addr_src));  // open: in2, in3
  RAM #(.addrWidth(16), .dataWidth(16), .bus("separate")) ram_1 (
    .addr(multiplexer_3_out), .din(multiplexer_2_out), .data(ram_1_data), .str(mem_write), .clk(CLOCK_out),
    .ld(not_1_out));  // open: sel, clr
  not not_1 (not_1_out, mem_write);
  ROM #(.dataWidth(16)) rom_1 (.addr(STATE_q), .data(rom_1_data));  // open: sel
  Multiplexer #(.select(2), .width(16)) multiplexer_4 (
    .in0({16{1'b0}}), .in1(16'h1), .in2(OPER_q), .out(multiplexer_4_out), .sel(B_src));  // open: in3
  Register #(.width(16)) OPER (.D(ram_1_data), .en(oper_write), .Q(OPER_q), .clk(CLOCK_out));  // open: clr
  alu alu_1 (
    .oper(ALU_op), .A(multiplexer_1_out), .B(multiplexer_4_out), .C_in(d_ff_1_q), .Z(alu_1_z),
    .Result(alu_1_result), .C_out(alu_1_c_out), .N(alu_1_n), .V(alu_1_v));
  Register #(.width(16)) IR (.D(ram_1_data), .en(IR_write), .Q(IR_q), .clk(CLOCK_out));  // open: clr
  Multiplexer #(.select(2), .width(16)) multiplexer_5 (
    .in0(ram_1_data), .in1(alu_1_result), .out(multiplexer_5_out), .sel(ACCUM_src));  // open: in2, in3
  Register #(.width(16)) ACCUM (.D(multiplexer_5_out), .en(ACCUM_write), .Q(ACCUM_q), .clk(CLOCK_out));  // open: clr
  D_Flip_Flop d_ff_1 (.clk(CLOCK_out), .D(alu_1_c_out), .Q(d_ff_1_q), .en(C_write));  // open: Qn, preset, reset
  Register #(.width(16)) X (.D(ram_1_data), .en(X_write), .Q(X_q), .clk(CLOCK_out));  // open: clr

  // Notes on the sheet:
  //   contents of rom_1 (hex, n*v repeats v):
  //   c000
endmodule

module alu (
  input  [3:0] oper,
  input  [15:0] A,
  input  [15:0] B,
  input  C_in,
  output Z,
  output [15:0] Result,
  output C_out,
  output N,
  output V
);

  wire adder_1_cout, subtractor_1_bout;
  wire [15:0] adder_1_out, subtractor_1_out;

  Adder #(.width(16)) adder_1 (.a(B), .b(A), .out(adder_1_out), .cin(C_in), .cout(adder_1_cout));
  Subtractor #(.width(16)) subtractor_1 (.a(A), .b(B), .out(subtractor_1_out), .bin(C_in), .bout(subtractor_1_bout));
  Multiplexer #(.select(4), .width(16)) multiplexer_1 (
    .in0(adder_1_out), .in1(subtractor_1_out), .out({N, Result[14:0]}), .sel(oper));  // open: in2, in3, in4, in5, in6, in7, in8, in9, in10, in11, in12, in13, in14, in15
  Multiplexer #(.select(4)) multiplexer_2 (
    .in0(adder_1_cout), .in1(subtractor_1_bout), .out(C_out), .sel(oper));  // open: in2, in3, in4, in5, in6, in7, in8, in9, in10, in11, in12, in13, in14, in15
  Pull_Resistor pull_resistor_1 (.node({N, Result[14:0]}));
  nor nor_1 (Z, Result[0], Result[1], Result[2], Result[3], Result[4], Result[5], Result[6], Result[7], Result[8], Result[9], Result[10], Result[11], Result[12], Result[13], Result[14], N);
  Pull_Resistor pull_resistor_2 (.node(C_out));
  overflow overflow_1 (.a(A[15]), .b(B[15]), .r(N), .v(V));
  Pull_Resistor pull_resistor_3 (.node(V));

  assign Result[15] = N;

  // Notes on the sheet:
  //   add adc, sbc and disable carry for add and sub
endmodule

module overflow (
  input  a,
  input  b,
  input  r,
  output v
);

  wire and_1_out, and_2_out, and_3_out, and_4_out, not_1_out, not_2_out, not_3_out;

  not not_1 (not_1_out, a);
  not not_2 (not_2_out, b);
  and and_1 (and_1_out, not_1_out, not_2_out);
  and and_2 (and_2_out, a, b);
  not not_3 (not_3_out, r);
  and and_3 (and_3_out, and_1_out, r);
  and and_4 (and_4_out, and_2_out, not_3_out);
  or or_1 (v, and_3_out, and_4_out);
endmodule

module \reg  (
  input  clock,
  input  dst_write,
  input  [3:0] src_select,
  input  [15:0] data_in,
  input  [3:0] dst_select,
  output [15:0] data_out,
  output [15:0] src_out,
  output [15:0] dst_out
);

  wire and_1_out, and_2_out, and_3_out, and_4_out, and_5_out, and_6_out, and_7_out, and_8_out,
       decoder_1_out0, decoder_1_out1, decoder_1_out2, decoder_1_out3, decoder_1_out4, decoder_1_out5,
       decoder_1_out6, decoder_1_out7, decoder_1_out8, decoder_2_out0, decoder_2_out1, decoder_2_out2,
       decoder_2_out3, decoder_2_out4, decoder_2_out5, decoder_2_out6, decoder_2_out7;
  wire [15:0] controlled_buffer_1_out, controlled_buffer_2_out, controlled_buffer_3_out,
       controlled_buffer_4_out, controlled_buffer_10_out, controlled_buffer_11_out, controlled_buffer_12_out,
       controlled_buffer_13_out, R0_q, R1_q, R2_q, R3_q, R4_q, R5_q, R6_q, R7_q;

  Decoder #(.select(4)) decoder_1 (
    .out0(decoder_1_out0), .out1(decoder_1_out1), .out2(decoder_1_out2), .out3(decoder_1_out3),
    .out4(decoder_1_out4), .out5(decoder_1_out5), .out6(decoder_1_out6), .out7(decoder_1_out7),
    .out8(decoder_1_out8), .sel(src_select));  // open: out9, out10, out11, out12, out13, out14, out15
  Decoder #(.select(4)) decoder_2 (
    .out0(decoder_2_out0), .out1(decoder_2_out1), .out2(decoder_2_out2), .out3(decoder_2_out3),
    .out4(decoder_2_out4), .out5(decoder_2_out5), .out6(decoder_2_out6), .out7(decoder_2_out7),
    .sel(dst_select));  // open: out8, out9, out10, out11, out12, out13, out14, out15
  and and_1 (and_1_out, dst_write, decoder_2_out0);
  and and_2 (and_2_out, dst_write, decoder_2_out1);
  and and_3 (and_3_out, dst_write, decoder_2_out2);
  and and_4 (and_4_out, dst_write, decoder_2_out3);
  assign controlled_buffer_1_out = decoder_2_out0 ? data_out : 16'bz;  // Controlled_Buffer controlled_buffer_1
  Register #(.width(16)) R0 (.D(controlled_buffer_1_out), .en(and_1_out), .Q(R0_q), .clk(clock));  // open: clr
  assign controlled_buffer_2_out = decoder_2_out1 ? data_out : 16'bz;  // Controlled_Buffer controlled_buffer_2
  Register #(.width(16)) R1 (.D(controlled_buffer_2_out), .en(and_2_out), .Q(R1_q), .clk(clock));  // open: clr
  assign controlled_buffer_3_out = decoder_2_out2 ? data_out : 16'bz;  // Controlled_Buffer controlled_buffer_3
  Register #(.width(16)) R2 (.D(controlled_buffer_3_out), .en(and_3_out), .Q(R2_q), .clk(clock));  // open: clr
  assign controlled_buffer_4_out = decoder_2_out3 ? data_out : 16'bz;  // Controlled_Buffer controlled_buffer_4
  Register #(.width(16)) R3 (.D(controlled_buffer_4_out), .en(and_4_out), .Q(R3_q), .clk(clock));  // open: clr
  assign data_out = decoder_1_out1 ? R1_q : 16'bz;  // Controlled_Buffer controlled_buffer_5
  assign data_out = decoder_1_out2 ? R2_q : 16'bz;  // Controlled_Buffer controlled_buffer_6
  assign data_out = decoder_1_out3 ? R3_q : 16'bz;  // Controlled_Buffer controlled_buffer_7
  assign data_out = decoder_1_out8 ? data_in : 16'bz;  // Controlled_Buffer controlled_buffer_8
  assign data_out = decoder_1_out0 ? R0_q : 16'bz;  // Controlled_Buffer controlled_buffer_9
  and and_5 (and_5_out, dst_write, decoder_2_out4);
  and and_6 (and_6_out, dst_write, decoder_2_out5);
  and and_7 (and_7_out, dst_write, decoder_2_out6);
  and and_8 (and_8_out, dst_write, decoder_2_out7);
  Register #(.width(16)) R4 (.D(controlled_buffer_10_out), .en(and_5_out), .Q(R4_q), .clk(clock));  // open: clr
  Register #(.width(16)) R5 (.D(controlled_buffer_11_out), .en(and_6_out), .Q(R5_q), .clk(clock));  // open: clr
  Register #(.width(16)) R6 (.D(controlled_buffer_12_out), .en(and_7_out), .Q(R6_q), .clk(clock));  // open: clr
  Register #(.width(16)) R7 (.D(controlled_buffer_13_out), .en(and_8_out), .Q(R7_q), .clk(clock));  // open: clr
  assign controlled_buffer_10_out = decoder_2_out4 ? data_out : 16'bz;  // Controlled_Buffer controlled_buffer_10
  assign controlled_buffer_11_out = decoder_2_out5 ? data_out : 16'bz;  // Controlled_Buffer controlled_buffer_11
  assign controlled_buffer_12_out = decoder_2_out6 ? data_out : 16'bz;  // Controlled_Buffer controlled_buffer_12
  assign controlled_buffer_13_out = decoder_2_out7 ? data_out : 16'bz;  // Controlled_Buffer controlled_buffer_13
  assign data_out = decoder_1_out4 ? R4_q : 16'bz;  // Controlled_Buffer controlled_buffer_14
  assign data_out = decoder_1_out5 ? R5_q : 16'bz;  // Controlled_Buffer controlled_buffer_15
  assign data_out = decoder_1_out6 ? R6_q : 16'bz;  // Controlled_Buffer controlled_buffer_16
  assign data_out = decoder_1_out7 ? R7_q : 16'bz;  // Controlled_Buffer controlled_buffer_17
  Multiplexer #(.select(4), .width(16)) multiplexer_1 (
    .in0(R0_q), .in1(R1_q), .in2(R2_q), .in3(R3_q), .in4(R4_q), .in5(R5_q), .in6(R6_q), .in7(R7_q),
    .in8(data_in), .out(src_out), .sel(src_select));  // open: in9, in10, in11, in12, in13, in14, in15
  Multiplexer #(.select(4), .width(16)) multiplexer_2 (
    .in0(R0_q), .in1(R1_q), .in2(R2_q), .in3(R3_q), .in4(R4_q), .in5(R5_q), .in6(R6_q), .in7(R7_q),
    .out(dst_out), .sel(dst_select));  // open: in8, in9, in10, in11, in12, in13, in14, in15
endmodule

module reg1 (
  input  [15:0] data_in,
  input  in_2,
  input  [2:0] src,
  input  [2:0] dst,
  input  in_5,
  input  write,
  input  [3:0] src_select,
  input  [3:0] dst_select,
  input  [15:0] in_9,
  input  [2:0] \reg ,
  input  [15:0] data_in_2,
  input  write_2,
  output [15:0] out_13,
  output [15:0] data_out,
  output [15:0] data_out_2
);

  wire clock_1_out, clock_2_out, clock_3_out, decoder_1_out0, decoder_1_out1, decoder_1_out2, decoder_1_out8,
       decoder_2_out0, decoder_2_out1, decoder_2_out2, not_1_out, not_2_out;
  wire [2:0] multiplexer_1_out;
  wire [15:0] controlled_buffer_1_out, controlled_buffer_2_out, controlled_buffer_3_out, multiplexer_2_out,
       R0_q, R1_q, R2_q, ram_1_data;

  Clock clock_1 (.out(clock_1_out));
  Decoder #(.select(4)) decoder_1 (
    .out0(decoder_1_out0), .out1(decoder_1_out1), .out2(decoder_1_out2), .out8(decoder_1_out8),
    .sel(src_select));  // open: out3, out4, out5, out6, out7, out9, out10, out11, out12, out13, out14, out15
  Decoder #(.select(4)) decoder_2 (
    .out0(decoder_2_out0), .out1(decoder_2_out1), .out2(decoder_2_out2), .sel(dst_select));  // open: out3, out4, out5, out6, out7, out8, out9, out10, out11, out12, out13, out14, out15
  assign controlled_buffer_1_out = decoder_2_out0 ? out_13 : 16'bz;  // Controlled_Buffer controlled_buffer_1
  Register #(.width(16)) R0 (
    .D(controlled_buffer_1_out), .en(decoder_2_out0), .Q(R0_q), .clk(clock_1_out));  // open: clr
  assign controlled_buffer_2_out = decoder_2_out1 ? out_13 : 16'bz;  // Controlled_Buffer controlled_buffer_2
  Register #(.width(16)) R1 (
    .D(controlled_buffer_2_out), .en(decoder_2_out1), .Q(R1_q), .clk(clock_1_out));  // open: clr
  assign controlled_buffer_3_out = decoder_2_out2 ? out_13 : 16'bz;  // Controlled_Buffer controlled_buffer_3
  Register #(.width(16)) R2 (
    .D(controlled_buffer_3_out), .en(decoder_2_out2), .Q(R2_q), .clk(clock_1_out));  // open: clr
  assign out_13 = decoder_1_out1 ? R1_q : 16'bz;  // Controlled_Buffer controlled_buffer_4
  assign out_13 = decoder_1_out2 ? R2_q : 16'bz;  // Controlled_Buffer controlled_buffer_5
  assign out_13 = decoder_1_out8 ? in_9 : 16'bz;  // Controlled_Buffer controlled_buffer_6
  assign out_13 = decoder_1_out0 ? R0_q : 16'bz;  // Controlled_Buffer controlled_buffer_7
  Clock clock_2 (.out(clock_2_out));
  Clock clock_3 (.out(clock_3_out));
  Multiplexer #(.width(3)) multiplexer_1 (.in0(src), .in1(dst), .out(multiplexer_1_out), .sel(in_5));
  Multiplexer #(.width(16)) multiplexer_2 (.in0(data_in), .in1(data_out), .out(multiplexer_2_out), .sel(in_2));
  not not_1 (not_1_out, write);
  not not_2 (not_2_out, write_2);
  RAM #(.addrWidth(3), .dataWidth(16), .bus("separate")) ram_1 (
    .addr(multiplexer_1_out), .din(multiplexer_2_out), .data(ram_1_data), .str(write), .clk(clock_3_out),
    .ld(not_1_out));  // open: sel, clr
  RAM #(.addrWidth(3), .dataWidth(16), .bus("separate")) ram_2 (
    .addr(\reg ), .din(data_in_2), .data(data_out_2), .str(write_2), .clk(clock_2_out), .ld(not_2_out));  // open: sel, clr
  Register #(.width(16)) register_1 (.D(ram_1_data), .Q(data_out), .clk(clock_3_out));  // open: en, clr
endmodule
